// Logisim project Four_way_multiplexer.circ as structural Verilog: 1 circuit, main circuit main
module main (
  input  Sel_0,
  input  Sel_1,
  input  A,
  input  B,
  input  C,
  input  D,
  output OUT
);

  wire and_1_out, and_2_out, and_3_out, and_4_out, not_1_out, not_2_out;

  not not_1 (not_1_out, Sel_0);
  not not_2 (not_2_out, Sel_1);
  and and_1 (and_1_out, A, not_2_out, not_1_out);
  and and_2 (and_2_out, B, not_2_out, Sel_0);
  and and_3 (and_3_out, C, Sel_1, not_1_out);
  and and_4 (and_4_out, D, Sel_1, Sel_0);
  or or_1 (OUT, and_1_out, and_2_out, and_3_out, and_4_out);

  // Notes on the sheet:
  //   多路复用器(4路)
endmodule
