// Logisim project Logic_gate_implemented_by_mosfet.circ as structural Verilog: 1 circuit, main circuit main
module main (
  input  in_1,
  input  in_2,
  output out_3,
  output out_4,
  output out_5,
  output out_6,
  output out_7,
  output out_8,
  output out_9,
  output out_10
);

  wire transistor_6_out, transistor_7_out, transistor_11_out;

  Transistor #(.\type ("n")) transistor_1 (.in(1'b1), .out(out_3), .gate(in_1));
  Transistor transistor_2 (.in(1'b0), .out(out_3), .gate(in_1));
  Transistor transistor_3 (.in(1'b1), .out(out_6), .gate(in_2));
  Transistor #(.gate("br")) transistor_4 (.in(1'b1), .out(out_6), .gate(in_1));
  Transistor #(.\type ("n")) transistor_5 (.in(transistor_6_out), .out(out_6), .gate(in_1));
  Transistor #(.\type ("n")) transistor_6 (.in(1'b0), .out(transistor_6_out), .gate(in_2));
  Transistor transistor_7 (.in(1'b1), .out(transistor_7_out), .gate(in_1));
  Transistor transistor_8 (.in(transistor_7_out), .out(out_8), .gate(in_2));
  Transistor #(.\type ("n"), .gate("br")) transistor_9 (.in(1'b0), .out(out_8), .gate(in_2));
  Transistor #(.\type ("n")) transistor_10 (.in(1'b0), .out(out_8), .gate(in_1));
  Transistor transistor_11 (.in(1'b1), .out(transistor_11_out), .gate(in_1));
  Transistor #(.\type ("n")) transistor_12 (.in(1'b0), .out(transistor_11_out), .gate(in_1));
  Transistor transistor_13 (.in(in_1), .out(out_9), .gate(in_2));
  Transistor #(.\type ("n")) transistor_14 (.in(transistor_11_out), .out(out_9), .gate(in_2));
  Transistor transistor_15 (.in(1'b1), .out(out_4), .gate(in_1));
  Transistor #(.\type ("n")) transistor_16 (.in(1'b0), .out(out_4), .gate(in_1));
  Transistor transistor_17 (.in(1'b1), .out(out_5), .gate(out_6));
  Transistor #(.\type ("n")) transistor_18 (.in(1'b0), .out(out_5), .gate(out_6));
  Transistor transistor_19 (.in(1'b1), .out(out_7), .gate(out_8));
  Transistor #(.\type ("n")) transistor_20 (.in(1'b0), .out(out_7), .gate(out_8));
  Transistor transistor_21 (.in(1'b1), .out(out_10), .gate(out_9));
  Transistor #(.\type ("n")) transistor_22 (.in(1'b0), .out(out_10), .gate(out_9));

  // Notes on the sheet:
  //   非门
  //   缓冲器
  //   与门(与非门+非门)
  //   与非门
  //   或门(或非门+非门)
  //   或非门
  //   异或门
  //   同或门(异或门+非门)
endmodule
