// Logisim project Registers.circ as structural Verilog: 1 circuit, main circuit main
module main (
  input  S,
  input  R,
  input  D,
  input  E,
  input  D_2,
  output out_6,
  output out_7,
  output Q,
  output _Q,
  output Q_2,
  output _Q_2
);

  wire and_1_out, buffer_1_out, clock_1_out, nand_1_out, nand_2_out, nand_5_out, nand_6_out, not_1_out;

  buf buffer_1 (buffer_1_out, clock_1_out);
  Clock clock_1 (.out(clock_1_out));
  nor nor_1 (out_6, S, out_7);
  nor nor_2 (out_7, out_6, R);
  nand nand_1 (nand_1_out, D, E);
  nand nand_2 (nand_2_out, nand_1_out, E);
  not not_1 (not_1_out, buffer_1_out);
  and and_1 (and_1_out, not_1_out, clock_1_out);
  nand nand_3 (Q, nand_1_out, _Q);
  nand nand_4 (_Q, Q, nand_2_out);
  nand nand_5 (nand_5_out, D_2, and_1_out);
  nand nand_6 (nand_6_out, nand_5_out, and_1_out);
  nand nand_7 (Q_2, nand_5_out, _Q_2);
  nand nand_8 (_Q_2, Q_2, nand_6_out);

  // Notes on the sheet:
  //   CLK
  //   S-R 锁存器
  //   DQ 锁存器
  //   DQ 触发器
endmodule
