// Logisim project risv_v_simple.circ as structural Verilog: 6 circuits, main circuit main
module main (
);

  wire ASel, BrEq, BrLt, BrUn, BSel, clock_1_out, clock_2_out, clock_3_out, MemRW, PCSel, RegWEn;
  wire [1:0] WBSel;
  wire [2:0] funct3;
  wire [3:0] ALUSel;
  wire [4:0] bit_extender_1_out, ImmSel, multiplier_1_out, rd, rs1, rs2;
  wire [6:0] funct7, opcode;
  wire [31:0] adder_1_out, alu_1_result, bit_extender_2_out, bit_extender_3_out, imm_gen_1_imm,
       multiplexer_1_out, multiplexer_2_out, multiplexer_3_out, multiplexer_4_out, multiplexer_5_out,
       ram_2_dout, reg_file_1_rs1_output, reg_file_1_rs2_output, register_1_q, shifter_1_out;

  Adder #(.width(32)) adder_1 (.a(register_1_q), .b(32'h4), .out(adder_1_out));  // open: cin, cout
  Register #(.width(32)) register_1 (.D(multiplexer_1_out), .en(1'b1), .clk(clock_1_out), .Q(register_1_q), .clr(1'b0));
  Multiplexer #(.width(32), .enable("false")) multiplexer_1 (
    .in0(adder_1_out), .in1(alu_1_result), .out(multiplexer_1_out), .sel(PCSel));
  Clock clock_1 (.out(clock_1_out));
  RAM #(.addrWidth(24), .dataWidth(32), .trigger("high")) ram_1 (
    .addr(register_1_q[25:2]), .we(1'b0), .oe(1'b1), .data({funct7, rs2, rs1, funct3, rd, opcode}));
  Multiplexer #(.select(2), .width(32), .enable("false")) multiplexer_2 (
    .in0(alu_1_result), .in1(multiplexer_5_out), .in2(register_1_q), .out(multiplexer_2_out), .sel(WBSel));  // open: in3
  control_unit control_unit_1 (
    .BSel(BSel), .ASel(ASel), .BrUn(BrUn), .ImmSel(ImmSel), .RegWEn(RegWEn), .PCSel(PCSel), .BrLt(BrLt),
    .BrEq(BrEq), .inst({funct7, rs2, rs1, funct3, rd, opcode}), .ALUSel(ALUSel), .MemRW(MemRW), .WBSel(WBSel));
  reg_file reg_file_1 (
    .rs1_input(rs1), .rs2_input(rs2), .rd(rd), .wb(multiplexer_2_out), .RegWEn(RegWEn), .Clock(clock_2_out),
    .rs1_output(reg_file_1_rs1_output), .rs2_output(reg_file_1_rs2_output));
  Clock clock_2 (.out(clock_2_out));
  imm_gen imm_gen_1 (.imm(imm_gen_1_imm), .inst({funct7, rs2, rs1, funct3, rd, opcode}), .immSel(ImmSel));
  branch_comp branch_comp_1 (
    .BrUn(BrUn), .BrLt(BrLt), .rs1(reg_file_1_rs1_output), .rs2(reg_file_1_rs2_output), .BrEq(BrEq));
  Multiplexer #(.width(32), .enable("false")) multiplexer_3 (
    .in0(reg_file_1_rs1_output), .in1(register_1_q), .out(multiplexer_3_out), .sel(ASel));
  Multiplexer #(.width(32), .enable("false")) multiplexer_4 (
    .in0(reg_file_1_rs2_output), .in1(imm_gen_1_imm), .out(multiplexer_4_out), .sel(BSel));
  ALU alu_1 (.ALUSel(ALUSel), .B(multiplexer_4_out), .A(multiplexer_3_out), .Result(alu_1_result));
  Clock clock_3 (.out(clock_3_out));
  RAM #(.addrWidth(14), .dataWidth(32), .trigger("falling"), .databus("bibus")) ram_2 (
    .addr(alu_1_result[15:2]), .we(MemRW), .oe(1'b1), .clk(clock_3_out), .din(reg_file_1_rs2_output),
    .dout(ram_2_dout));
  assign bit_extender_1_out = {{3{1'b0}}, alu_1_result[1:0]};  // Bit_Extender bit_extender_1
  Multiplier #(.width(5)) multiplier_1 (
    .a(bit_extender_1_out), .b(5'b01110), .out(multiplier_1_out));  // open: cin, cout
  Shifter #(.width(32), .shift("lr")) shifter_1 (.in(ram_2_dout), .\dist (multiplier_1_out), .out(shifter_1_out));
  assign bit_extender_2_out = {{24{shifter_1_out[7]}}, shifter_1_out[7:0]};  // Bit_Extender bit_extender_2
  assign bit_extender_3_out = {{16{shifter_1_out[15]}}, shifter_1_out[15:0]};  // Bit_Extender bit_extender_3
  Multiplexer #(.select(3), .width(32), .enable("false")) multiplexer_5 (
    .in0(bit_extender_2_out), .in1(bit_extender_3_out), .in2(shifter_1_out), .out(multiplexer_5_out),
    .sel(funct3));  // open: in3, in4, in5, in6, in7

  // Notes on the sheet:
  //   PC输出线
  //   IF Instruction Fetch
  //   输出到PC自己, Reg File, ALU的A端口
  //   指令内存不需要时钟信号输入, 直接高电平激活即可
  //   Write Back输出线
  //   ALU输出线
  //   ID Instruction Decode
  //   Write Back意思是从内存写入寄存器
  //   从ALU输出到PC或别的寄存器或WB(作为WB的偏移量)
  //   是否以无符号模式比较
  //   DRAM读写
  //   0 PC继续自增, 1 PC改为ALU的输出值
  //   寄存器允许写入
  //   因为不同的指令类型imm有分段
  //   0 从rs1输入, 1 从PC输入
  //   0 从rs2输入, 1 从立即数输入
  //   alu计算(输出)模式
  //   0 从alu输入, 1 从wb输入, 2 从PC输入
  //   到ALU
  //   到Reg File
  //   所以根据对应的指令type进行对应的解析处理
  //   EX Execution
  //   rs2(即B)具有保存到数据内存中的能力
  //   MEM Memory Operation
  //   数据内存下降沿更新
  //   分别对应lb, lh, lw
  //   lb, lh, lw这三个指令可用funct3区分
  //   WB Write Back
endmodule

module reg_file (
  input  [4:0] rs1_input,
  input  [4:0] rs2_input,
  input  [4:0] rd,
  input  [31:0] wb,
  input  RegWEn,
  input  Clock,
  output [31:0] rs1_output,
  output [31:0] rs2_output
);

  wire and_1_out, and_2_out, and_3_out, and_4_out, and_5_out, and_6_out, and_7_out, and_8_out,
       decoder_1_out1, decoder_1_out2, decoder_1_out5, decoder_1_out6, decoder_1_out7, decoder_1_out8,
       decoder_1_out9, decoder_1_out10;
  wire [31:0] a0, ra, s0, s1, sp, t0, t1, t2;

  Decoder #(.select(5), .enable("false")) decoder_1 (
    .out1(decoder_1_out1), .out2(decoder_1_out2), .out5(decoder_1_out5), .out6(decoder_1_out6),
    .out7(decoder_1_out7), .out8(decoder_1_out8), .out9(decoder_1_out9), .out10(decoder_1_out10), .sel(rd));  // open: out0, out3, out4, out11, out12, out13, out14, out15, out16, out17, out18, out19, out20, out21, out22, out23, out24, out25, out26, out27, out28, out29, out30, out31
  and and_1 (and_1_out, decoder_1_out1, RegWEn);
  and and_2 (and_2_out, decoder_1_out2, RegWEn);
  and and_3 (and_3_out, decoder_1_out5, RegWEn);
  and and_4 (and_4_out, decoder_1_out6, RegWEn);
  and and_5 (and_5_out, decoder_1_out7, RegWEn);
  and and_6 (and_6_out, decoder_1_out8, RegWEn);
  and and_7 (and_7_out, decoder_1_out9, RegWEn);
  and and_8 (and_8_out, decoder_1_out10, RegWEn);
  Register #(.width(32)) register_1 (.D(wb), .en(and_1_out), .clk(Clock), .Q(ra));  // open: clr
  Register #(.width(32)) register_2 (.D(wb), .en(and_2_out), .clk(Clock), .Q(sp));  // open: clr
  Register #(.width(32)) register_3 (.D(wb), .en(and_3_out), .clk(Clock), .Q(t0));  // open: clr
  Register #(.width(32)) register_4 (.D(wb), .en(and_4_out), .clk(Clock), .Q(t1));  // open: clr
  Register #(.width(32)) register_5 (.D(wb), .en(and_5_out), .clk(Clock), .Q(t2));  // open: clr
  Register #(.width(32)) register_6 (.D(wb), .en(and_6_out), .clk(Clock), .Q(s0));  // open: clr
  Register #(.width(32)) register_7 (.D(wb), .en(and_7_out), .clk(Clock), .Q(s1));  // open: clr
  Register #(.width(32)) register_8 (.D(wb), .en(and_8_out), .clk(Clock), .Q(a0));  // open: clr
  Multiplexer #(.select(5), .width(32), .enable("false")) multiplexer_1 (
    .in0({32{1'b0}}), .in1(ra), .in2(sp), .in5(t0), .in6(t1), .in7(t2), .in8(s0), .in9(s1), .in10(a0),
    .out(rs1_output), .sel(rs2_input));  // open: in3, in4, in11, in12, in13, in14, in15, in16, in17, in18, in19, in20, in21, in22, in23, in24, in25, in26, in27, in28, in29, in30, in31
  Multiplexer #(.select(5), .width(32), .enable("false")) multiplexer_2 (
    .in0({32{1'b0}}), .in1(ra), .in2(sp), .in5(t0), .in6(t1), .in7(t2), .in8(s0), .in9(s1), .in10(a0),
    .out(rs2_output), .sel(rs1_input));  // open: in3, in4, in11, in12, in13, in14, in15, in16, in17, in18, in19, in20, in21, in22, in23, in24, in25, in26, in27, in28, in29, in30, in31

  // Other names for the same wires on the sheet: clk = Clock; read_data1[31:0] = rs1_output;
  //   read_data2[31:0] = rs2_output; read_reg1[4:0] = rs1_input; read_reg2[4:0] = rs2_input; write_data[31:0] = wb;
  //   write_en = RegWEn; write_reg[4:0] = rd
endmodule

module ALU (
  input  [31:0] A,
  input  [31:0] B,
  input  [3:0] ALUSel,
  output [31:0] Result
);

  wire comparator_2_lt, xor_2_out;
  wire [31:0] adder_1_out, and_1_out, bit_extender_1_out, divider_1_out, divider_1_rem, multiplexer_1_out,
       multiplexer_2_out, multiplexer_4_out, multiplier_1_cout, multiplier_1_out, multiplier_2_cout,
       negator_1_out, negator_2_out, not_1_out, or_1_out, shifter_1_out, shifter_2_out, shifter_3_out,
       xor_1_out;

  Comparator comparator_1 ();  // open: a, b, gt, eq, lt
  Adder #(.width(32)) adder_1 (.a(A), .b(B), .out(adder_1_out));  // open: cin, cout
  assign and_1_out = A & B;  // AND_Gate and_1, 32 bits wide
  assign or_1_out = A | B;  // OR_Gate or_1, 32 bits wide
  assign xor_1_out = A ^ B;  // XOR_Gate xor_1, 32 bits wide
  Shifter #(.width(32), .shift("lr")) shifter_1 (.in(A), .\dist (B[4:0]), .out(shifter_1_out));
  Shifter #(.width(32), .shift("ar")) shifter_2 (.in(A), .\dist (B[4:0]), .out(shifter_2_out));
  Shifter #(.width(32)) shifter_3 (.in(A), .\dist (B[4:0]), .out(shifter_3_out));
  Comparator #(.width(32)) comparator_2 (.a(A), .b(B), .lt(comparator_2_lt));  // open: gt, eq
  Divider #(.width(32)) divider_1 (.a(A), .b(B), .out(divider_1_out), .rem(divider_1_rem));  // open: upper
  Multiplier #(.width(32)) multiplier_1 (.a(A), .b(B), .out(multiplier_1_out), .cout(multiplier_1_cout));  // open: cin
  Subtractor #(.width(32)) subtractor_1 (.a(A), .b(B));  // open: out, bin, bout
  Negator #(.width(32)) negator_1 (.in(B), .out(negator_1_out));
  Negator #(.width(32)) negator_2 (.in(A), .out(negator_2_out));
  assign bit_extender_1_out = {{31{1'b0}}, comparator_2_lt};  // Bit_Extender bit_extender_1
  Multiplexer #(.width(32), .enable("false")) multiplexer_1 (
    .in0(B), .in1(negator_1_out), .out(multiplexer_1_out), .sel(B[31]));
  Multiplexer #(.width(32), .enable("false")) multiplexer_2 (
    .in0(A), .in1(negator_2_out), .out(multiplexer_2_out), .sel(A[31]));
  xor xor_2 (xor_2_out, B[31], A[31]);
  Multiplier #(.width(32)) multiplier_2 (
    .a(multiplexer_1_out), .b(multiplexer_2_out), .cout(multiplier_2_cout));  // open: out, cin
  assign not_1_out = ~multiplier_2_cout;  // NOT_Gate not_1, 32 bits wide
  Multiplexer #(.select(4), .width(32), .enable("false")) multiplexer_3 (
    .in0(adder_1_out), .in1(and_1_out), .in2(or_1_out), .in3(xor_1_out), .in4(shifter_1_out),
    .in5(shifter_2_out), .in6(shifter_3_out), .in7(bit_extender_1_out), .in8(divider_1_out),
    .in9(divider_1_rem), .in10(multiplier_1_out), .in11(multiplier_1_cout), .in12(B), .out(Result),
    .sel(ALUSel));  // open: in13, in14, in15
  Multiplexer #(.width(32), .enable("false")) multiplexer_4 (
    .in0(multiplier_2_cout), .in1(not_1_out), .out(multiplexer_4_out), .sel(xor_2_out));
  // AND_Gate and_2 has open pins: in0=multiplexer_4_out, out=open

  // Other names for the same wires on the sheet: ALU_select[3:0] = ALUSel

  // Notes on the sheet:
  //   如果是负数先转换为正数
  //   如果有一个数是负数
  //   那就按位取反
endmodule

module imm_gen (
  input  [4:0] immSel,
  input  [31:0] inst,
  output [31:0] imm
);

  wire [31:0] and_1_out, and_2_out, and_3_out, and_4_out, and_5_out, bit_extender_1_out, bit_extender_2_out,
       bit_extender_3_out, bit_extender_4_out, bit_extender_5_out, bit_extender_6_out, bit_extender_7_out,
       bit_extender_8_out, bit_extender_9_out;

  assign bit_extender_1_out = {{31{immSel[0]}}, immSel[0]};  // Bit_Extender bit_extender_1
  assign bit_extender_2_out = {{20{inst[31]}}, inst[31:20]};  // Bit_Extender bit_extender_2
  assign bit_extender_3_out = {{31{immSel[1]}}, immSel[1]};  // Bit_Extender bit_extender_3
  assign bit_extender_4_out = {{20{inst[31]}}, {inst[31:25], inst[11:7]}};  // Bit_Extender bit_extender_4
  assign bit_extender_5_out = {{31{immSel[2]}}, immSel[2]};  // Bit_Extender bit_extender_5
  assign bit_extender_6_out = {{19{inst[31]}}, {inst[31], inst[7], inst[30:25], inst[11:8], 1'b0}};  // Bit_Extender bit_extender_6
  assign bit_extender_7_out = {{31{immSel[3]}}, immSel[3]};  // Bit_Extender bit_extender_7
  assign bit_extender_8_out = {{31{immSel[4]}}, immSel[4]};  // Bit_Extender bit_extender_8
  assign bit_extender_9_out = {{11{inst[31]}}, {inst[31], inst[19:12], inst[20], inst[30:21], 1'b0}};  // Bit_Extender bit_extender_9
  assign and_1_out = bit_extender_1_out & bit_extender_2_out;  // AND_Gate and_1, 32 bits wide
  assign and_2_out = bit_extender_3_out & bit_extender_4_out;  // AND_Gate and_2, 32 bits wide
  assign and_3_out = bit_extender_5_out & bit_extender_6_out;  // AND_Gate and_3, 32 bits wide
  assign and_4_out = bit_extender_7_out & {inst[31:12], {12{1'b0}}};  // AND_Gate and_4, 32 bits wide
  assign and_5_out = bit_extender_8_out & bit_extender_9_out;  // AND_Gate and_5, 32 bits wide
  assign imm = and_1_out | and_2_out | and_3_out | and_4_out | and_5_out;  // OR_Gate or_1, 32 bits wide

  // Other names for the same wires on the sheet: instruction[31:0] = inst; immediate_select[4:0] = immSel;
  //   immediate_value[31:0] = imm

  // Notes on the sheet:
  //   因为SB类型没有捕获imm的0位, 所以手动补0
  //   根据Core Instruction Formats来设计
  //   I类型指令
  //   20-31 imm
  //   S类型指令
  //   7-11 imm[4:0]
  //   25-31 imm[11:5]
  //   SB类型指令
  //   内容较多, 具体看CIF表
  //   U类型指令
  //   参考上面SB的解释
  //   UJ类型指令
endmodule

module branch_comp (
  input  [31:0] rs1,
  input  [31:0] rs2,
  input  BrUn,
  output BrEq,
  output BrLt
);

  wire comparator_1_eq, comparator_1_lt, comparator_2_eq, comparator_2_lt;

  Comparator #(.width(32)) comparator_1 (.a(rs1), .b(rs2), .eq(comparator_1_eq), .lt(comparator_1_lt));  // open: gt
  Comparator #(.width(32), .mode("unsigned")) comparator_2 (
    .a(rs1), .b(rs2), .eq(comparator_2_eq), .lt(comparator_2_lt));  // open: gt
  Multiplexer #(.enable("false")) multiplexer_1 (.in0(comparator_1_eq), .in1(comparator_2_eq), .out(BrEq), .sel(BrUn));
  Multiplexer #(.enable("false")) multiplexer_2 (.in0(comparator_1_lt), .in1(comparator_2_lt), .out(BrLt), .sel(BrUn));

  // Other names for the same wires on the sheet: A[31:0] = rs1; B[31:0] = rs2; branch_equal = BrEq;
  //   branch_less_than = BrLt; branch_unsigned = BrUn

  // Notes on the sheet:
  //   signed
  //   unsigned
endmodule

module control_unit (
  input  [31:0] inst,
  input  BrEq,
  input  BrLt,
  output PCSel,
  output RegWEn,
  output [4:0] ImmSel,
  output BrUn,
  output ASel,
  output BSel,
  output [3:0] ALUSel,
  output MemRW,
  output [1:0] WBSel
);

  wire add, addi, and_9_out, and_10_out, and_11_out, and_12_out, and_13_out, and_14_out, and_15_out,
       and_16_out, and_17_out, and_18_out, and_19_out, and_20_out, and_21_out, and_22_out, and_23_out,
       and_1080616f, andi, beq, blt, bne, div, divu, I, I_jalr, I_Load, lb, lh, lw, mul, mulh, mulhu,
       or_4_out, or_5_out, or_6_out, or_7_out, or_8_out, or_9_out, or_10_out, or_11_out, or_12_out,
       or_483976f9, ori, R, rem_90254230, remu, sll_a5a2ae92, slli, slt, slti, srai, srl_04da4a0d, srli, sub,
       xor_e25a1cfa, xori;
  wire [1:0] transistor_1_out, transistor_3_out, transistor_5_out;
  wire [3:0] transistor_7_out, transistor_9_out, transistor_11_out, transistor_13_out, transistor_15_out,
       transistor_17_out, transistor_19_out, transistor_21_out, transistor_23_out, transistor_25_out,
       transistor_27_out, transistor_29_out, transistor_31_out;

  and and_1 (R, inst[0], inst[1], ~inst[2], ~inst[3], inst[4], inst[5], ~inst[6]);  // AND_Gate
  and and_2 (I_Load, inst[0], inst[1], ~inst[2], ~inst[3], ~inst[4], ~inst[5], ~inst[6]);  // AND_Gate
  and and_3 (I, inst[0], inst[1], ~inst[2], ~inst[3], inst[4], ~inst[5], ~inst[6]);  // AND_Gate
  and and_4 (ImmSel[1], inst[0], inst[1], ~inst[2], ~inst[3], ~inst[4], inst[5], ~inst[6]);  // AND_Gate
  and and_5 (ImmSel[2], inst[0], inst[1], ~inst[2], ~inst[3], ~inst[4], inst[5], inst[6]);  // AND_Gate
  and and_6 (ImmSel[3], inst[0], inst[1], inst[2], ~inst[3], inst[4], inst[5], ~inst[6]);  // AND_Gate
  and and_7 (ImmSel[4], inst[0], inst[1], inst[2], inst[3], ~inst[4], inst[5], inst[6]);  // AND_Gate
  and and_8 (I_jalr, inst[0], inst[1], inst[2], ~inst[3], ~inst[4], inst[5], inst[6]);  // AND_Gate
  and and_9 (and_9_out, ~inst[12], ~inst[13], ~inst[14]);  // AND_Gate
  and and_10 (and_10_out, inst[12], ~inst[13], ~inst[14]);  // AND_Gate
  and and_11 (and_11_out, ~inst[12], inst[13], ~inst[14]);  // AND_Gate
  and and_12 (and_12_out, inst[12], inst[13], ~inst[14]);  // AND_Gate
  and and_13 (and_13_out, ~inst[12], ~inst[13], inst[14]);  // AND_Gate
  and and_14 (and_14_out, inst[12], ~inst[13], inst[14]);  // AND_Gate
  and and_15 (and_15_out, ~inst[12], inst[13], inst[14]);  // AND_Gate
  and and_16 (and_16_out, inst[12], inst[13], inst[14]);
  and and_17 (and_17_out, ~inst[25], ~inst[26], ~inst[27], ~inst[28], ~inst[29], ~inst[30], ~inst[31]);  // AND_Gate
  and and_18 (and_18_out, inst[25], ~inst[26], ~inst[27], ~inst[28], ~inst[29], ~inst[30], ~inst[31]);  // AND_Gate
  and and_19 (and_19_out, ~inst[25], ~inst[26], ~inst[27], ~inst[28], ~inst[29], inst[30], ~inst[31]);  // AND_Gate
  and and_20 (and_20_out, BrEq, beq);
  and and_21 (and_21_out, ~BrEq, bne);  // AND_Gate
  and and_22 (and_22_out, BrLt, blt);
  and and_23 (and_23_out, BrLt, BrUn);
  or or_1 (PCSel, and_20_out, and_21_out, and_22_out, and_23_out, ImmSel[4], I_jalr);
  and and_24 (add, R, and_9_out, and_17_out);
  and and_25 (mul, R, and_9_out, and_18_out);
  and and_26 (sub, R, and_9_out, and_19_out);
  and and_27 (sll_a5a2ae92, R, and_10_out, and_17_out);
  and and_28 (mulh, R, and_10_out, and_18_out);
  and and_29 (slt, R, and_11_out, and_17_out);
  and and_30 (mulhu, R, and_12_out, and_18_out);
  and and_31 (xor_e25a1cfa, R, and_13_out, and_17_out);
  and and_32 (div, R, and_13_out, and_18_out);
  and and_33 (divu, R, and_14_out, and_18_out);
  and and_34 (srl_04da4a0d, R, and_14_out, and_17_out);
  and and_35 (or_483976f9, R, and_15_out, and_17_out);
  and and_36 (rem_90254230, R, and_15_out, and_18_out);
  and and_37 (remu, R, and_16_out, and_18_out);
  and and_38 (and_1080616f, R, and_16_out, and_17_out);
  and and_39 (lb, I_Load, and_9_out);
  and and_40 (lh, I_Load, and_10_out);
  and and_41 (lw, I_Load, and_11_out);
  and and_42 (addi, I, and_9_out);
  and and_43 (slli, I, and_10_out, and_17_out);
  and and_44 (slti, I, and_11_out);
  and and_45 (xori, I, and_13_out);
  and and_46 (srli, I, and_14_out, and_17_out);
  and and_47 (srai, I, and_14_out, and_19_out);
  and and_48 (ori, I, and_15_out);
  and and_49 (andi, I, and_16_out);
  and and_50 (beq, ImmSel[2], and_9_out);
  and and_51 (bne, ImmSel[2], and_10_out);
  and and_52 (blt, ImmSel[2], and_13_out);
  and and_53 (BrUn, ImmSel[2], and_15_out);
  or or_2 (ImmSel[0], I_Load, I, I_jalr);
  nor nor_1 (RegWEn, ImmSel[1], beq, bne, blt, BrUn);
  // OR_Gate or_3 has open pins: in0=I_Load, in1=I_jalr, in2=ImmSel[4], in3=ImmSel[1], in4=add, in5=addi, in6=ImmSel[2], out=open
  or or_4 (or_4_out, and_1080616f, andi);
  or or_5 (or_5_out, or_483976f9, ori);
  or or_6 (or_6_out, xor_e25a1cfa, xori);
  or or_7 (or_7_out, srli, srl_04da4a0d);
  or or_8 (or_8_out, slli, sll_a5a2ae92);
  or or_9 (or_9_out, slt, slti);
  or or_10 (or_10_out, R, I);
  or or_11 (or_11_out, lb, lh, lw);
  or or_12 (or_12_out, ImmSel[4], I_jalr);
  not not_1 (BSel, R);
  Transistor #(.\type ("n"), .width(2)) transistor_1 (.in(2'b00), .out(transistor_1_out), .gate(or_10_out));
  Transistor #(.gate("br"), .width(2)) transistor_2 (.in(2'b00), .out(transistor_1_out), .gate(or_10_out));
  Transistor #(.\type ("n"), .width(2)) transistor_3 (.in(2'b01), .out(transistor_3_out), .gate(or_11_out));
  Transistor #(.gate("br"), .width(2)) transistor_4 (.in(2'b00), .out(transistor_3_out), .gate(or_11_out));
  Transistor #(.\type ("n"), .width(2)) transistor_5 (.in(2'b10), .out(transistor_5_out), .gate(or_12_out));
  Transistor #(.gate("br"), .width(2)) transistor_6 (.in(2'b00), .out(transistor_5_out), .gate(or_12_out));
  Transistor #(.\type ("n"), .width(4)) transistor_7 (.in(4'b0001), .out(transistor_7_out), .gate(or_4_out));
  Transistor #(.gate("br"), .width(4)) transistor_8 (.in(4'b0000), .out(transistor_7_out), .gate(or_4_out));
  Transistor #(.\type ("n"), .width(4)) transistor_9 (.in(4'b0010), .out(transistor_9_out), .gate(or_5_out));
  Transistor #(.gate("br"), .width(4)) transistor_10 (.in(4'b0000), .out(transistor_9_out), .gate(or_5_out));
  Transistor #(.\type ("n"), .width(4)) transistor_11 (.in(4'b0011), .out(transistor_11_out), .gate(or_6_out));
  Transistor #(.gate("br"), .width(4)) transistor_12 (.in(4'b0000), .out(transistor_11_out), .gate(or_6_out));
  Transistor #(.\type ("n"), .width(4)) transistor_13 (.in(4'b0100), .out(transistor_13_out), .gate(or_7_out));
  Transistor #(.gate("br"), .width(4)) transistor_14 (.in(4'b0000), .out(transistor_13_out), .gate(or_7_out));
  Transistor #(.\type ("n"), .width(4)) transistor_15 (.in(4'b0101), .out(transistor_15_out), .gate(srai));
  Transistor #(.gate("br"), .width(4)) transistor_16 (.in(4'b0000), .out(transistor_15_out), .gate(srai));
  Transistor #(.\type ("n"), .width(4)) transistor_17 (.in(4'b0110), .out(transistor_17_out), .gate(or_8_out));
  Transistor #(.gate("br"), .width(4)) transistor_18 (.in(4'b0000), .out(transistor_17_out), .gate(or_8_out));
  Transistor #(.\type ("n"), .width(4)) transistor_19 (.in(4'b0111), .out(transistor_19_out), .gate(or_9_out));
  Transistor #(.gate("br"), .width(4)) transistor_20 (.in(4'b0000), .out(transistor_19_out), .gate(or_9_out));
  Transistor #(.\type ("n"), .width(4)) transistor_21 (.in(4'b1000), .out(transistor_21_out), .gate(div));
  Transistor #(.gate("br"), .width(4)) transistor_22 (.in(4'b0000), .out(transistor_21_out), .gate(div));
  Transistor #(.\type ("n"), .width(4)) transistor_23 (.in(4'b1001), .out(transistor_23_out), .gate(rem_90254230));
  Transistor #(.gate("br"), .width(4)) transistor_24 (.in(4'b0000), .out(transistor_23_out), .gate(rem_90254230));
  Transistor #(.\type ("n"), .width(4)) transistor_25 (.in(4'b1010), .out(transistor_25_out), .gate(mul));
  Transistor #(.gate("br"), .width(4)) transistor_26 (.in(4'b0000), .out(transistor_25_out), .gate(mul));
  Transistor #(.\type ("n"), .width(4)) transistor_27 (.in(4'b1011), .out(transistor_27_out), .gate(mulh));
  Transistor #(.gate("br"), .width(4)) transistor_28 (.in(4'b0000), .out(transistor_27_out), .gate(mulh));
  Transistor #(.\type ("n"), .width(4)) transistor_29 (.in(4'b1100), .out(transistor_29_out), .gate(sub));
  Transistor #(.gate("br"), .width(4)) transistor_30 (.in(4'b0000), .out(transistor_29_out), .gate(sub));
  Transistor #(.\type ("n"), .width(4)) transistor_31 (.in(4'b1101), .out(transistor_31_out), .gate(ImmSel[3]));
  Transistor #(.gate("br"), .width(4)) transistor_32 (.in(4'b0000), .out(transistor_31_out), .gate(ImmSel[3]));
  or or_13 (ASel, beq, bne, blt, BrUn, ImmSel[3], ImmSel[4]);
  assign WBSel = transistor_1_out | transistor_3_out | transistor_5_out;  // OR_Gate or_14, 2 bits wide
  assign ALUSel = transistor_7_out | transistor_9_out | transistor_11_out | transistor_13_out | transistor_15_out | transistor_17_out | transistor_19_out | transistor_21_out | transistor_23_out | transistor_25_out | transistor_27_out | transistor_29_out | transistor_31_out;  // OR_Gate or_15, 4 bits wide

  assign MemRW = ImmSel[1];

  // Other names for the same wires on the sheet: A_select = ASel; ALU_select[3:0] = ALUSel; B_select = BSel;
  //   branch_equal = BrEq; branch_less_than = BrLt; bltu = BrUn; branch_unsigned = BrUn;
  //   immediate_value_select[4:0] = ImmSel; memory_read_write = ImmSel[1]; S_sw = ImmSel[1]; SB = ImmSel[2];
  //   U_lui = ImmSel[3]; UJ_jal = ImmSel[4]; instruction[31:0] = inst; opcode[6:0] = inst[6:0];
  //   funct3[2:0] = inst[14:12]; funct7[6:0] = inst[31:25]; PC_select = PCSel; reg_write_enable = RegWEn;
  //   write_back_select[1:0] = WBSel

  // Notes on the sheet:
  //   如sw
  //   类型下只有一个指令的直接用opcode检测的tunnel代替
  //   0 PC继续自增, 1 PC改为ALU的输出值
  //   寄存器允许写入
  //   因为不同的指令类型imm有分段
  //   是否以无符号模式比较
  //   0 从rs1输入, 1 从PC输入
  //   0 从rs2输入, 1 从立即数输入
  //   alu模式
  //   DRAM读写
  //   0 从alu输入, 1 从wb输入, 2 从PC输入
  //   到ALU
  //   到Reg File
  //   0x33
  //   0x03
  //   0x13
  //   0x23
  //   0x63
  //   0x37
  //   0x6f
  //   0x67
  //   所以根据对应的指令type进行对应的解析处理
  //   I_Load有多个指令
  //   0x0
  //   0x1
  //   0x2
  //   0x3
  //   0x4
  //   0x5
  //   0x6
  //   0x7
  //   0x00
  //   0x01
  //   0x20
  //   div R  funct3 0x4 funct7 0x01
  //   rem R funct3 0x6 funct7 0x01
  //   配合我的奇怪设计imm_gen
  //   lb, lh, lw是1(WB)
  //   R和I全是0 (ALU输入) 
  //   UJ_jal和I_jalr是2(PC)
  //   lui好像不需要这个
  //   建议去掉
  //   没有实现divu
  //   TODO: 用n型transistor代替
  //   默认就是0, 不需要触发
  //   0000
  //   0000
  //   0000
  //   0000
  //   0000
  //   0000
  //   0000
  //   0000
  //   0000
  //   0000
  //   0000
  //   0000
  //   0010
  //   0011
  //   0011
  //   0110
  //   0001
  //   0001
  //   0010
  //   0100
  //   0100
  //   0101
  //   0110
  //   0111
  //   0111
  //   1000
  //   1001
  //   1010
  //   1011
  //   1100
  //   1101
endmodule
